# Fritzing sketch IR-Learner (saved by Fritzing 0.9.10b)
breadboards: 1

parts:
  Part1 = Arduino Nano (Rev3.0) (ICSP)
  D1 = LTE-302 [package=lte-302]
  IR1 = TSOP312.., 314.. [package=THT]
  R1 = Rotary Potentiometer (Large) [maximum_resistance=100kΩ knob_status=50% power=0.5W package=THT]
  S2 = Momentary Switch [package=ksa_sealed_tac_switch]
  R2 = Resistor [tolerance=±5% resistance=220 package="1206 [SMD]"]

nets:
  N1: Part1.GND, IR1.Vs, R1.leg1, S2.1, R2.Pin_0
  N2: Part1.D2, D1.C
  N3: Part1.D3, S2.3
  N4: Part1.D4, IR1.GND
  N5: Part1.5V, IR1.Data, R1.leg2
  N6: Part1.A1, R1.wiper
  N7: D1.A, R2.Pin_1
