# Fritzing sketch NEC (saved by Fritzing 0.9.10b)
breadboards: 1

parts:
  Part1 = Arduino Nano (Rev3.0) (ICSP)
  D1 = LTE-302 [package=lte-302]
  IR1 = TSOP312.., 314.. [package=THT]
  S2 = Momentary Switch [package=ksa_sealed_tac_switch]
  R2 = Resistor [tolerance=±5% resistance=220 package="1206 [SMD]"]
  S3 = Momentary Switch [package=ksa_sealed_tac_switch]
  S4 = Momentary Switch [package=ksa_sealed_tac_switch]
  Grove1 = Grove OLED 128x96
  BAT1 = BC9VPC [package=bc9vpc]

nets:
  GND: Part1.GND, IR1.Vs, S2.1, R2.Pin_0, S3.1, S4.1, Grove1.GND, BAT1.V-
  N1: Part1.D2, D1.C
  N2: Part1.D4, IR1.GND, S2.3
  N3: Part1.D5, S3.3
  N4: Part1.D8, S4.3
  N5: Part1.VIN, BAT1.V+
  5V: Part1.5V, IR1.Data, Grove1.VCC
  N6: Part1.A5, Grove1.SCL
  N7: Part1.A4, Grove1.SDA
  N8: D1.A, R2.Pin_1
